# Fritzing sketch Metal Detector (saved by Fritzing 0.9.3b)

parts:
  C1 = Ceramic Capacitor [capacitance=100nF package="100 mil [THT, multilayer]"]
  D1 = Rectifier Diode [part_number=1N4001 package="300 mil [THT]"]
  L1 = Inductor [package="400 mil [THT]"]
  Part1 = Arduino Uno (Rev3)
  R1 = Resistor [tolerance=±5% resistance=220 package=THT]
  R2 = Resistor [tolerance=±5% resistance=220 package=THT]
  LED1 = smd LED [color="Red (633nm)" package="1206 [SMD]"]
  SG1 = Buzzer 12mm [package=buzzer-ccv-kit]

nets:
  N1: C1.0, L1.pin_0, Part1.GND, LED1.cathode, SG1.1
  N2: C1.1, D1.cathode, Part1.A2
  N3: Part1.A1, R1.Pin_1
  N4: Part1.D9_PWM, SG1.2
  N5: Part1.D10_PWM/SS, R2.Pin_0
