# Fritzing sketch Motor Driver (saved by Fritzing 0.9.3b)

parts:
  Part1 = Adafruit Motor/Stepper/Servo Shield [part_number="Adafruit #1438"]
  M1 = DC Motor
  M2 = DC Motor
  M3 = DC Motor
  M4 = DC Motor
  VCC1 = Battery block 9V
  J1 = Basic Servo

nets:
  N1: Part1.M2A, M4.pin_1
  N2: Part1.M2B, M4.pin_2
  N3: Part1.M1B, M3.pin_1
  N4: Part1.M1A, M3.pin_2
  N5: Part1.M3A, M1.pin_2
  N6: Part1.M3B, M1.pin_1
  N7: Part1.M4B, M2.pin_2
  N8: Part1.M4A, M2.pin_1
  GND: Part1.GND, VCC1.-, J1.gnd
  N9: Part1.VMOTOR, VCC1.+
  +5V: Part1.+5V, J1.vcc
  N10: Part1.D10, J1.pulse

custom parts:
  Adafruit Motor/Stepper/Servo Shield: The original Adafruit Motorshield kit is one of our most beloved kits, which is why we decided to make something even better. We have upgraded the shield kit to make the bestest, easiest way to drive DC and Stepper motors. This shield will make quick work of your next robotics project! We kept the ability to drive up to 4 DC motors or 2 stepper motors, but added many improvements: Instead of a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
